// Logisim project mmarc-one-logic-array.circ as structural Verilog: 2 circuits, main circuit main
module main (
);

  wire and_1_out, bitselector_1_out, bitselector_2_out, bitselector_3_out, button_1_out, clock_1_out,
       clock_2_out, comparator_1_eq, datapath_logic_1_accum_write, datapath_logic_1_alu_op,
       datapath_logic_1_alu_src, datapath_logic_1_branch, datapath_logic_1_imm_sel, datapath_logic_1_in_sel,
       datapath_logic_1_mem_sel, datapath_logic_1_offset_en, datapath_logic_1_read_en,
       datapath_logic_1_write_en, datapath_logic_1_write_sel, not_1_out, not_2_out;
  wire [2:0] bit_extender_1_out;
  wire [3:0] bitselector_4_out, bitselector_5_out, bitselector_6_out, bitselector_7_out;
  wire [12:0] adder_1_out, adder_2_out, bit_extender_2_out, bit_extender_5_out, bit_extender_7_out,
       multiplexer_1_out, multiplexer_4_out, multiplexer_5_out, multiplexer_6_out, multiplexer_9_out, PC_q,
       ram_1_data, ReadOutput_q;
  wire [15:0] Accumulator_q, adder_3_out, bit_extender_3_out, bit_extender_4_out, bit_extender_6_out,
       multiplexer_2_out, multiplexer_3_out, multiplexer_7_out, multiplexer_8_out, rom_1_data, shifter_1_out,
       subtractor_1_out;

  Shifter #(.width(16), .shift("lr")) shifter_1 (.in(rom_1_data), .\dist (4'b1101), .out(shifter_1_out));
  Bit_Extender #(.in_width(16), .out_width(3)) bit_extender_1 (.in(shifter_1_out), .out(bit_extender_1_out));
  BitSelector #(.width(3)) bitselector_1 (.in(bit_extender_1_out), .out(bitselector_1_out), .sel(2'b10));
  BitSelector #(.width(3)) bitselector_2 (.in(bit_extender_1_out), .out(bitselector_2_out), .sel(2'b01));
  BitSelector #(.width(3)) bitselector_3 (.in(bit_extender_1_out), .out(bitselector_3_out), .sel(2'b00));
  Clock #(.highDuration(2), .lowDuration(2)) clock_1 (.out(clock_1_out));
  Register #(.width(13)) PC (.D(multiplexer_1_out), .en(1'b1), .Q(PC_q), .clk(clock_1_out), .clr(button_1_out));
  Button button_1 (.out(button_1_out));
  Adder #(.width(13)) adder_1 (.a(13'h1), .b(PC_q), .out(adder_1_out));  // open: cin, cout
  Adder #(.width(13)) adder_2 (.a(adder_1_out), .b(bit_extender_2_out), .out(adder_2_out));  // open: cin, cout
  Multiplexer #(.width(13), .enable("false")) multiplexer_1 (
    .in0(adder_1_out), .in1(adder_2_out), .out(multiplexer_1_out), .sel(and_1_out));
  datapath_logic datapath_logic_1 (
    .b2(bitselector_1_out), .b1(bitselector_2_out), .b0(bitselector_3_out), .branch(datapath_logic_1_branch),
    .mem_sel(datapath_logic_1_mem_sel), .read_en(datapath_logic_1_read_en),
    .write_en(datapath_logic_1_write_en), .accum_write(datapath_logic_1_accum_write),
    .alu_op(datapath_logic_1_alu_op), .alu_src(datapath_logic_1_alu_src), .in_sel(datapath_logic_1_in_sel),
    .imm_sel(datapath_logic_1_imm_sel), .offset_en(datapath_logic_1_offset_en),
    .write_sel(datapath_logic_1_write_sel));
  ROM #(.addrWidth(13), .dataWidth(16)) rom_1 (.addr(PC_q), .data(rom_1_data), .sel(1'b1));
  and and_1 (and_1_out, comparator_1_eq, datapath_logic_1_branch);
  Bit_Extender #(.in_width(16), .out_width(13)) bit_extender_2 (.in(rom_1_data), .out(bit_extender_2_out));
  assign bit_extender_3_out = {{3{bit_extender_2_out[12]}}, bit_extender_2_out};  // Bit_Extender bit_extender_3
  Register #(.width(16)) Accumulator (
    .D(multiplexer_7_out), .en(datapath_logic_1_accum_write), .Q(Accumulator_q), .clk(clock_1_out));  // open: clr
  Multiplexer #(.width(16), .enable("false")) multiplexer_2 (
    .in0(bit_extender_3_out), .in1(bit_extender_4_out), .out(multiplexer_2_out),
    .sel(datapath_logic_1_alu_src));
  assign bit_extender_4_out = {{3{ram_1_data[12]}}, ram_1_data};  // Bit_Extender bit_extender_4
  Multiplexer #(.width(16), .enable("false")) multiplexer_3 (
    .in0(multiplexer_8_out), .in1(bit_extender_6_out), .out(multiplexer_3_out), .sel(datapath_logic_1_mem_sel));
  Adder #(.width(16)) adder_3 (.a(Accumulator_q), .b(multiplexer_2_out), .out(adder_3_out));  // open: cin, cout
  Subtractor #(.width(16)) subtractor_1 (
    .a(Accumulator_q), .b(multiplexer_2_out), .out(subtractor_1_out));  // open: bin, bout
  Multiplexer #(.width(13), .enable("false")) multiplexer_4 (
    .in0(bit_extender_2_out), .in1(bit_extender_5_out), .out(multiplexer_4_out),
    .sel(datapath_logic_1_offset_en));
  Multiplexer #(.width(13), .enable("false")) multiplexer_5 (
    .in0(multiplexer_4_out), .in1(multiplexer_6_out), .out(multiplexer_5_out), .sel(not_1_out));
  not not_1 (not_1_out, clock_2_out);
  Multiplexer #(.width(13), .enable("false")) multiplexer_6 (
    .in0(bit_extender_2_out), .in1(bit_extender_7_out), .out(multiplexer_6_out),
    .sel(datapath_logic_1_write_sel));
  Multiplexer #(.width(16), .enable("false")) multiplexer_7 (
    .in0(multiplexer_3_out), .in1(bit_extender_3_out), .out(multiplexer_7_out), .sel(datapath_logic_1_imm_sel));
  Multiplexer #(.width(16), .enable("false")) multiplexer_8 (
    .in0(adder_3_out), .in1(subtractor_1_out), .out(multiplexer_8_out), .sel(datapath_logic_1_alu_op));
  Bit_Extender #(.in_width(16), .out_width(13), .\type ("sign")) bit_extender_5 (
    .in(multiplexer_8_out), .out(bit_extender_5_out));
  Comparator #(.width(16)) comparator_1 (.a(Accumulator_q), .b({16{1'b0}}), .eq(comparator_1_eq));  // open: gt, lt
  RAM #(.addrWidth(13), .dataWidth(13), .bus("separate")) ram_1 (
    .addr(multiplexer_5_out), .din(multiplexer_9_out), .data(ram_1_data), .str(datapath_logic_1_write_en),
    .sel(1'b1), .clk(clock_2_out), .ld(datapath_logic_1_read_en));  // open: clr
  Multiplexer #(.width(13), .enable("false")) multiplexer_9 (
    .in0(bit_extender_7_out), .in1(ReadOutput_q), .out(multiplexer_9_out), .sel(datapath_logic_1_in_sel));
  assign bit_extender_6_out = {{3{ram_1_data[12]}}, ram_1_data};  // Bit_Extender bit_extender_6
  Register #(.width(13)) ReadOutput (
    .D(ram_1_data), .en(datapath_logic_1_read_en), .Q(ReadOutput_q), .clk(not_2_out));  // open: clr
  Hex_Digit_Display hex_digit_display_1 (.value(bitselector_4_out));  // open: dp
  BitSelector #(.width(16), .group(4)) bitselector_4 (.in(Accumulator_q), .out(bitselector_4_out), .sel(2'b11));
  not not_2 (not_2_out, clock_2_out);
  Bit_Extender #(.in_width(16), .out_width(13), .\type ("sign")) bit_extender_7 (
    .in(Accumulator_q), .out(bit_extender_7_out));
  Clock clock_2 (.out(clock_2_out));
  Hex_Digit_Display hex_digit_display_2 (.value(bitselector_5_out));  // open: dp
  BitSelector #(.width(16), .group(4)) bitselector_5 (.in(Accumulator_q), .out(bitselector_5_out), .sel(2'b10));
  Hex_Digit_Display hex_digit_display_3 (.value(bitselector_6_out));  // open: dp
  BitSelector #(.width(16), .group(4)) bitselector_6 (.in(Accumulator_q), .out(bitselector_6_out), .sel(2'b01));
  Hex_Digit_Display hex_digit_display_4 (.value(bitselector_7_out));  // open: dp
  BitSelector #(.width(16), .group(4)) bitselector_7 (.in(Accumulator_q), .out(bitselector_7_out), .sel(2'b00));

  // Notes on the sheet:
  //   b2
  //   b1
  //   b0
  //   Instruction Memory
  //   contents of rom_1 (hex, n*v repeats v):
  //   c000 e000 1e c000 e001 e000 4004 c000 e002 e000 a004 4004 c000 e003 2004 c000 e001 8001 4001 c000
  //   e002 8001 4002 c000 e003 8001 4003 c000 e000 9fff 4000 c000 1fdf 1fff
  //   Branch
  //   mem sel
  //   write en
  //   accum write
  //   alu op
  //   in sel
  //   imm sel
  //   offset en
  //   read en
  //   alu src
  //   write sel
  //   Write en
  //   alu sel
  //   mem sel
  //   offset en
  //   write sel
  //   imm sel
  //   0 - read, 1 -write
  //   alu op
  //   zero
  //   in sel
endmodule

module datapath_logic (
  input  b2,
  input  b1,
  input  b0,
  output branch,
  output mem_sel,
  output read_en,
  output write_en,
  output accum_write,
  output alu_op,
  output alu_src,
  output in_sel,
  output imm_sel,
  output offset_en,
  output write_sel
);

  wire and_3_out, and_4_out, and_5_out, and_6_out, not_1_out;

  not not_1 (not_1_out, b0);
  not not_2 (in_sel, b1);
  not not_3 (alu_op, b2);
  and and_1 (branch, alu_op, in_sel, not_1_out);
  and and_2 (mem_sel, b2, b1);
  and and_3 (and_3_out, alu_op, in_sel, b0);
  and and_4 (and_4_out, alu_op, b1, not_1_out);
  and and_5 (and_5_out, b1, b0);
  and and_6 (and_6_out, b0, in_sel);
  and and_7 (imm_sel, not_1_out, b1);
  and and_8 (offset_en, b2, b1);
  or or_1 (write_en, and_3_out, and_4_out);
  or or_2 (accum_write, and_5_out, b2);
  or or_3 (alu_src, and_6_out, alu_op);

  assign read_en = b0;
  assign write_sel = in_sel;
endmodule
